// Logisim project cpu.circ as structural Verilog: 2 circuits, main circuit main
module main (
  input  [31:0] INSTRUCTION,
  input  CLOCK,
  output [31:0] FETCH_ADDRESS,
  output [31:0] s0_Value,
  output [31:0] s1_Value,
  output [31:0] t0_Value,
  output [31:0] t1_Value,
  output [31:0] a0_Value,
  output [31:0] ra_Value,
  output [31:0] sp_Value
);

  wire Add, addASel, addBSel, Addi, addiASel, addiMemRW, addiPCSel, addMemRW, addPCSel, And, and_1_out,
       and_2_out, and_4_out, and_5_out, and_6_out, and_7_out, and_8_out, and_9_out, and_10_out, and_11_out,
       and_13_out, and_14_out, and_15_out, and_16_out, andASel, andBSel, Andi, andiASel, andiMemRW,
       andiPCSel, andMemRW, andPCSel, ASel, Beq, BeqMemRW, BeqPCSel, BeqRegWEn, Blt, BltMemRW, BltPCSel,
       BltRegWEn, Bltu, BltuMemRW, BltuPCSel, BltuRegWEn, brEQ, brLT, BSel, comparator_1_eq, comparator_1_lt,
       comparator_2_eq, comparator_2_lt, demultiplexer_4_out0, demultiplexer_5_out0, demultiplexer_6_out0,
       Div, divASel, divBSel, divMemRW, divPCSel, Jal, JalMemRW, Jalr, JalrASel, JalrMemRW, Lb, lbASel,
       lbMemRW, lbPCSel, Lh, lhASel, lhMemRW, lhPCSel, Lui, LuiASel, LuiMemRW, LuiPCSel, lwASel, lwMemRW,
       lwPCSel, MEM_p1, MEM_p2, MEM_p4, MEM_p10, MemRW, Mul, mulASel, mulBSel, MulH, mulhASel, mulhBSel,
       mulhMemRW, mulhPCSel, mulMemRW, mulPCSel, NegSel, not_52_out, not_53_out, not_54_out, not_55_out,
       not_62_out, not_66_out, not_70_out, not_83_out, not_87_out, not_91_out, not_95_out, not_101_out,
       not_104_out, Or, or_6_out, or_8_out, or_9_out, or_10_out, orASel, orBSel, Ori, oriASel, oriMemRW,
       oriPCSel, orMemRW, orPCSel, PCSel, RegWEn, Rem, remASel, remBSel, remMemRW, remPCSel, Sll, sllASel,
       sllBSel, Slli, slliASel, slliMemRW, slliPCSel, sllMemRW, sllPCSel, Slt, sltASel, sltBSel, Slti,
       sltiASel, sltiMemRW, sltiPCSel, sltMemRW, sltPCSel, Srl, srlASel, srlBSel, Srli, srliASel, srliMemRW,
       srliPCSel, srlMemRW, srlPCSel, subASel, subBSel, subMemRW, subPCSel, Sw, SwASel, SwPCSel, SwRegWEn,
       Xor, xorASel, xorBSel, Xori, xoriASel, xoriMemRW, xoriPCSel, xorMemRW, xorPCSel;
  wire [1:0] addiWBSel, addWBSel, andiWBSel, andWBSel, BeqWBSel, bit_extender_53_out, bit_extender_54_out,
       bit_extender_65_out, BltuWBSel, BltWBSel, divWBSel, JalrWBSel, JalWBSel, lbWBSel, lhWBSel, LuiWBSel,
       lwWBSel, mulhWBSel, mulWBSel, oriWBSel, orWBSel, remWBSel, slliWBSel, sllWBSel, sltiWBSel, sltWBSel,
       srliWBSel, srlWBSel, subWBSel, SwWBSel, WBSel, xoriWBSel, xorWBSel;
  wire [2:0] addiImmSel, andiImmSel, BeqiImmSel, bit_extender_51_out, bit_extender_58_out,
       bit_extender_74_out, bit_extender_75_out, bit_extender_76_out, BltiImmSel, BltuiImmSel, ImmSel,
       JaliImmSel, JalrImmSel, lbImmSel, lhImmSel, LuiiImmSel, lwImmSel, oriImmSel, shifter_20_out,
       slliImmSel, sltiImmSel, srliImmSel, swImmSel, xoriImmSel;
  wire [3:0] addALUSel, addiALUSel, ALUSel, andALUSel, andiALUSel, BeqALUSel, bit_extender_1_out,
       bit_extender_3_out, bit_extender_5_out, bit_extender_7_out, bit_extender_9_out, bit_extender_11_out,
       bit_extender_13_out, bit_extender_15_out, bit_extender_19_out, bit_extender_21_out,
       bit_extender_23_out, bit_extender_29_out, bit_extender_31_out, bit_extender_33_out,
       bit_extender_35_out, bit_extender_39_out, bit_extender_41_out, bit_extender_46_out,
       bit_extender_55_out, bit_extender_59_out, bit_extender_61_out, bit_extender_62_out,
       bit_extender_64_out, bit_extender_66_out, bit_extender_68_out, bit_extender_72_out,
       bit_extender_77_out, BltALUSel, BltuALUSel, divALUSel, JalALUSel, JalrALUSel, lbALUSel, lhALUSel,
       LuiALUSel, lwALUSel, mulALUSel, mulhALUSel, orALUSel, oriALUSel, remALUSel, shifter_2_out,
       shifter_4_out, shifter_5_out, shifter_6_out, shifter_7_out, shifter_8_out, shifter_10_out,
       shifter_12_out, shifter_13_out, shifter_15_out, shifter_16_out, shifter_18_out, shifter_19_out,
       sllALUSel, slliALUSel, sltALUSel, sltiALUSel, srlALUSel, srliALUSel, subALUSel, SwALUSel, xorALUSel,
       xoriALUSel;
  wire [24:0] Iimm, SBimm, Simm, Uimm, UJimm;
  wire [31:0] adder_1_out, bit_extender_25_out, bit_extender_26_out, bit_extender_27_out,
       bit_extender_28_out, demultiplexer_1_out0, demultiplexer_1_out1, demultiplexer_2_out0,
       demultiplexer_2_out1, immGen, main_2_result, MEM_p11, multiplexer_1_out, multiplexer_9_out,
       multiplexer_10_out, multiplexer_11_out, multiplexer_12_out, multiplexer_14_out, negator_1_out, R1, R2;

  Multiplexer #(.width(32)) multiplexer_1 (
    .in0(adder_1_out), .in1(main_2_result), .out(multiplexer_1_out), .sel(PCSel));  // open: en
  Register #(.width(32)) PC (.D(multiplexer_1_out), .Q(FETCH_ADDRESS), .clk(CLOCK));  // open: en, clr
  not not_1 (addPCSel, Add);
  not not_2 (addASel, Add);
  not not_3 (addBSel, Add);
  assign bit_extender_1_out = {{3{1'b0}}, Add};  // Bit_Extender bit_extender_1
  not not_4 (addMemRW, Add);
  assign addWBSel = {{1{1'b0}}, Add};  // Bit_Extender bit_extender_2
  not not_5 (mulPCSel, Mul);
  not not_6 (mulASel, Mul);
  not not_7 (mulBSel, Mul);
  assign bit_extender_3_out = {{3{1'b0}}, Mul};  // Bit_Extender bit_extender_3
  not not_8 (mulMemRW, Mul);
  assign mulWBSel = {{1{1'b0}}, Mul};  // Bit_Extender bit_extender_4
  not not_9 (subPCSel, NegSel);
  not not_10 (subASel, NegSel);
  not not_11 (subBSel, NegSel);
  assign bit_extender_5_out = {{3{1'b0}}, NegSel};  // Bit_Extender bit_extender_5
  not not_12 (subMemRW, NegSel);
  assign subWBSel = {{1{1'b0}}, NegSel};  // Bit_Extender bit_extender_6
  not not_13 (sllPCSel, Sll);
  not not_14 (sllASel, Sll);
  not not_15 (sllBSel, Sll);
  assign bit_extender_7_out = {{3{1'b0}}, Sll};  // Bit_Extender bit_extender_7
  not not_16 (sllMemRW, Sll);
  assign sllWBSel = {{1{1'b0}}, Sll};  // Bit_Extender bit_extender_8
  not not_17 (mulhPCSel, MulH);
  not not_18 (mulhASel, MulH);
  not not_19 (mulhBSel, MulH);
  assign bit_extender_9_out = {{3{1'b0}}, MulH};  // Bit_Extender bit_extender_9
  not not_20 (mulhMemRW, MulH);
  assign mulhWBSel = {{1{1'b0}}, MulH};  // Bit_Extender bit_extender_10
  not not_21 (sltPCSel, Slt);
  not not_22 (sltASel, Slt);
  not not_23 (sltBSel, Slt);
  assign bit_extender_11_out = {{3{1'b0}}, Slt};  // Bit_Extender bit_extender_11
  not not_24 (sltMemRW, Slt);
  assign sltWBSel = {{1{1'b0}}, Slt};  // Bit_Extender bit_extender_12
  not not_25 (xorPCSel, Xor);
  not not_26 (xorASel, Xor);
  not not_27 (xorBSel, Xor);
  assign bit_extender_13_out = {{3{1'b0}}, Xor};  // Bit_Extender bit_extender_13
  not not_28 (xorMemRW, Xor);
  assign xorWBSel = {{1{1'b0}}, Xor};  // Bit_Extender bit_extender_14
  not not_29 (divPCSel, Div);
  not not_30 (divASel, Div);
  not not_31 (divBSel, Div);
  assign bit_extender_15_out = {{3{1'b0}}, Div};  // Bit_Extender bit_extender_15
  not not_32 (divMemRW, Div);
  assign divWBSel = {{1{1'b0}}, Div};  // Bit_Extender bit_extender_16
  not not_33 (srlPCSel, Srl);
  not not_34 (srlASel, Srl);
  not not_35 (srlBSel, Srl);
  assign srlALUSel = {{3{1'b0}}, Srl};  // Bit_Extender bit_extender_17
  not not_36 (srlMemRW, Srl);
  assign srlWBSel = {{1{1'b0}}, Srl};  // Bit_Extender bit_extender_18
  not not_37 (orPCSel, Or);
  not not_38 (orASel, Or);
  not not_39 (orBSel, Or);
  assign bit_extender_19_out = {{3{1'b0}}, Or};  // Bit_Extender bit_extender_19
  not not_40 (orMemRW, Or);
  assign orWBSel = {{1{1'b0}}, Or};  // Bit_Extender bit_extender_20
  not not_41 (remPCSel, Rem);
  not not_42 (remASel, Rem);
  not not_43 (remBSel, Rem);
  assign bit_extender_21_out = {{3{1'b0}}, Rem};  // Bit_Extender bit_extender_21
  not not_44 (remMemRW, Rem);
  assign remWBSel = {{1{1'b0}}, Rem};  // Bit_Extender bit_extender_22
  not not_45 (andPCSel, And);
  not not_46 (andASel, And);
  not not_47 (andBSel, And);
  assign bit_extender_23_out = {{3{1'b0}}, And};  // Bit_Extender bit_extender_23
  not not_48 (andMemRW, And);
  assign andWBSel = {{1{1'b0}}, And};  // Bit_Extender bit_extender_24
  Adder #(.width(32)) adder_1 (.a(FETCH_ADDRESS), .b(32'h4), .out(adder_1_out));  // open: cin, cout
  Shifter #(.width(4)) shifter_1 (.in(bit_extender_1_out), .\dist (2'b01), .out(addALUSel));
  and and_1 (and_1_out, brEQ, Beq);
  assign bit_extender_25_out = {{20{1'b0}}, Iimm[24:13]};  // Bit_Extender bit_extender_25
  assign bit_extender_26_out = {{20{1'b0}}, {Simm[24:18], Simm[4:0]}};  // Bit_Extender bit_extender_26
  assign bit_extender_27_out = {{19{1'b0}}, {SBimm[24], SBimm[0], SBimm[23:18], SBimm[4:1], 1'b0}};  // Bit_Extender bit_extender_27
  assign bit_extender_28_out = {{11{1'b0}}, {UJimm[24], UJimm[12:5], UJimm[13], UJimm[23:14], 1'b0}};  // Bit_Extender bit_extender_28
  Shifter #(.width(4)) shifter_2 (.in(bit_extender_3_out), .\dist (2'b10), .out(shifter_2_out));
  Shifter #(.width(4)) shifter_3 (.in(bit_extender_9_out), .\dist (2'b11), .out(mulhALUSel));
  Shifter #(.width(4)) shifter_4 (.in(bit_extender_11_out), .\dist (2'b01), .out(shifter_4_out));
  Shifter #(.width(4)) shifter_5 (.in(bit_extender_13_out), .\dist (2'b10), .out(shifter_5_out));
  Shifter #(.width(4)) shifter_6 (.in(bit_extender_15_out), .\dist (2'b11), .out(shifter_6_out));
  Shifter #(.width(4)) shifter_7 (.in(bit_extender_23_out), .\dist (2'b01), .out(shifter_7_out));
  and and_2 (and_2_out, Blt, brLT);
  Demultiplexer #(.width(32)) demultiplexer_1 (
    .out0(demultiplexer_1_out0), .out1(demultiplexer_1_out1), .in(R1), .en(Bltu));  // open: sel
  Demultiplexer #(.width(32)) demultiplexer_2 (
    .out0(demultiplexer_2_out0), .out1(demultiplexer_2_out1), .in(R2), .en(Bltu));  // open: sel
  assign mulALUSel = bit_extender_3_out | shifter_2_out | shifter_8_out;  // OR_Gate or_1, 4 bits wide
  Shifter #(.width(4)) shifter_8 (.in(bit_extender_3_out), .\dist (2'b01), .out(shifter_8_out));
  Shifter #(.width(4)) shifter_9 (.in(bit_extender_5_out), .\dist (2'b01), .out(subALUSel));
  assign sllALUSel = bit_extender_7_out & 4'b0000;  // AND_Gate and_3, 4 bits wide
  assign sltALUSel = shifter_4_out | shifter_10_out;  // OR_Gate or_2, 4 bits wide
  Shifter #(.width(4)) shifter_10 (.in(bit_extender_11_out), .\dist (2'b10), .out(shifter_10_out));
  assign xorALUSel = bit_extender_13_out | shifter_5_out;  // OR_Gate or_3, 4 bits wide
  assign divALUSel = bit_extender_15_out | shifter_6_out;  // OR_Gate or_4, 4 bits wide
  Shifter #(.width(4)) shifter_11 (.in(bit_extender_19_out), .\dist (2'b10), .out(orALUSel));
  Shifter #(.width(4)) shifter_12 (.in(bit_extender_21_out), .\dist (2'b01), .out(shifter_12_out));
  Shifter #(.width(4)) shifter_13 (.in(bit_extender_21_out), .\dist (2'b11), .out(shifter_13_out));
  assign andALUSel = bit_extender_23_out | shifter_7_out;  // OR_Gate or_5, 4 bits wide
  Multiplexer multiplexer_2 (.in0(1'b0), .in1(1'b1), .out(PCSel), .sel(or_6_out));  // open: en
  or or_6 (or_6_out, and_1_out, and_2_out, and_4_out, Jal, Jalr);
  and and_4 (and_4_out, Bltu, brLT);
  Demultiplexer #(.select(3), .width(25)) demultiplexer_3 (
    .out0(Iimm), .out1(Simm), .out2(SBimm), .out3(Uimm), .out4(UJimm), .in(INSTRUCTION[31:7]), .sel(ImmSel));  // open: out5, out6, out7, en
  Multiplexer #(.select(3), .width(32)) multiplexer_3 (
    .in0(bit_extender_25_out), .in1(bit_extender_26_out), .in2(bit_extender_27_out),
    .in3({Uimm[24:5], {12{1'b0}}}), .in4(bit_extender_28_out), .out(immGen), .sel(ImmSel));  // open: in5, in6, in7, en
  Comparator #(.width(32)) comparator_1 (
    .a(demultiplexer_1_out0), .b(demultiplexer_2_out0), .eq(comparator_1_eq), .lt(comparator_1_lt));  // open: gt
  Comparator #(.width(32), .mode("unsigned")) comparator_2 (
    .a(demultiplexer_1_out1), .b(demultiplexer_2_out1), .eq(comparator_2_eq), .lt(comparator_2_lt));  // open: gt
  assign remALUSel = shifter_12_out | shifter_13_out;  // OR_Gate or_7, 4 bits wide
  or or_8 (or_8_out, Addi, Slli, Slti, Xori, Srli, Ori, Andi, Lui, Lb, Lb, Lh, Sw, Beq, Blt, Bltu, Jal, Jalr);
  Multiplexer multiplexer_4 (.in0(1'b0), .in1(1'b1), .out(RegWEn), .sel(or_9_out));  // open: en
  or or_9 (or_9_out, Add, Mul, NegSel, Sll, MulH, Slt, Xor, Div, Srl, Or, Rem, And, Addi, Slli, Slti, Xori, Srli, Ori, Andi, Lui, Lb, Lb, Lh, Jal, Jalr);
  Multiplexer multiplexer_5 (.in0(comparator_1_eq), .in1(comparator_2_eq), .out(brEQ), .sel(Bltu));  // open: en
  Multiplexer multiplexer_6 (.in0(comparator_1_lt), .in1(comparator_2_lt), .out(brLT), .sel(Bltu));  // open: en
  not not_49 (addiPCSel, Addi);
  not not_50 (addiASel, Addi);
  assign bit_extender_29_out = {{3{1'b0}}, Addi};  // Bit_Extender bit_extender_29
  not not_51 (addiMemRW, Addi);
  assign addiWBSel = {{1{1'b0}}, Addi};  // Bit_Extender bit_extender_30
  not not_52 (not_52_out, Addi);
  not not_53 (not_53_out, Slli);
  not not_54 (not_54_out, Ori);
  not not_55 (not_55_out, Andi);
  Multiplexer multiplexer_7 (.in0(1'b0), .in1(1'b1), .out(BSel), .sel(or_8_out));  // open: en
  regfile_main main_1 (
    .Read_Register_1__rs1(INSTRUCTION[19:15]), .Read_Register_2__rs2(INSTRUCTION[24:20]),
    .Write_Register__rd(INSTRUCTION[11:7]), .Write_Data(multiplexer_14_out), .Write_Enable(RegWEn),
    .Clock(CLOCK), .Read_Data_1(R1), .Read_Data_2(R2), .s1_Value(s1_Value), .t0_Value(t0_Value),
    .t1_Value(t1_Value), .a0_Value(a0_Value), .s0_Value(s0_Value), .ra_Value(ra_Value), .sp_Value(sp_Value));
  and and_5 (and_5_out, not_52_out, Addi);
  not not_56 (slliPCSel, Slli);
  not not_57 (slliASel, Slli);
  assign bit_extender_31_out = {{3{1'b0}}, Slli};  // Bit_Extender bit_extender_31
  not not_58 (slliMemRW, Slli);
  assign slliWBSel = {{1{1'b0}}, Slli};  // Bit_Extender bit_extender_32
  not not_59 (sltiPCSel, Slti);
  not not_60 (sltiASel, Slti);
  assign bit_extender_33_out = {{3{1'b0}}, Slti};  // Bit_Extender bit_extender_33
  not not_61 (sltiMemRW, Slti);
  assign sltiWBSel = {{1{1'b0}}, Slti};  // Bit_Extender bit_extender_34
  not not_62 (not_62_out, Slti);
  not not_63 (xoriPCSel, Xori);
  not not_64 (xoriASel, Xori);
  assign bit_extender_35_out = {{3{1'b0}}, Xori};  // Bit_Extender bit_extender_35
  not not_65 (xoriMemRW, Xori);
  assign xoriWBSel = {{1{1'b0}}, Xori};  // Bit_Extender bit_extender_36
  not not_66 (not_66_out, Xori);
  not not_67 (srliPCSel, Srli);
  not not_68 (srliASel, Srli);
  assign srliALUSel = {{3{1'b0}}, Srli};  // Bit_Extender bit_extender_37
  not not_69 (srliMemRW, Srli);
  assign srliWBSel = {{1{1'b0}}, Srli};  // Bit_Extender bit_extender_38
  not not_70 (not_70_out, Srli);
  not not_71 (oriPCSel, Ori);
  not not_72 (oriASel, Ori);
  assign bit_extender_39_out = {{3{1'b0}}, Ori};  // Bit_Extender bit_extender_39
  not not_73 (oriMemRW, Ori);
  assign oriWBSel = {{1{1'b0}}, Ori};  // Bit_Extender bit_extender_40
  not not_74 (andiPCSel, Andi);
  not not_75 (andiASel, Andi);
  assign bit_extender_41_out = {{3{1'b0}}, Andi};  // Bit_Extender bit_extender_41
  not not_76 (andiMemRW, Andi);
  assign andiWBSel = {{1{1'b0}}, Andi};  // Bit_Extender bit_extender_42
  Shifter #(.width(4)) shifter_14 (.in(bit_extender_29_out), .\dist (2'b01), .out(addiALUSel));
  assign addiImmSel = {{2{1'b0}}, and_5_out};  // Bit_Extender bit_extender_43
  assign slliImmSel = {{2{1'b0}}, and_6_out};  // Bit_Extender bit_extender_44
  and and_6 (and_6_out, not_53_out, Slli);
  and and_7 (and_7_out, not_62_out, Slti);
  and and_8 (and_8_out, not_66_out, Xori);
  and and_9 (and_9_out, not_70_out, Srli);
  and and_10 (and_10_out, not_54_out, Ori);
  assign andiImmSel = {{2{1'b0}}, and_11_out};  // Bit_Extender bit_extender_45
  and and_11 (and_11_out, not_55_out, Andi);
  assign bit_extender_46_out = {{3{1'b0}}, Lui};  // Bit_Extender bit_extender_46
  not not_77 (LuiPCSel, Lui);
  Multiplexer multiplexer_8 (.in0(1'b0), .in1(1'b1), .out(ASel), .sel(or_10_out));  // open: en
  or or_10 (or_10_out, Beq, Blt, Bltu, Jal);
  Multiplexer #(.width(32)) multiplexer_9 (.in0(R2), .in1(immGen), .out(multiplexer_9_out), .sel(BSel));  // open: en
  assign slliALUSel = bit_extender_31_out & 4'b0000;  // AND_Gate and_12, 4 bits wide
  Shifter #(.width(4)) shifter_15 (.in(bit_extender_33_out), .\dist (2'b01), .out(shifter_15_out));
  assign sltiImmSel = {{2{1'b0}}, and_7_out};  // Bit_Extender bit_extender_47
  Shifter #(.width(4)) shifter_16 (.in(bit_extender_35_out), .\dist (2'b10), .out(shifter_16_out));
  assign xoriImmSel = {{2{1'b0}}, and_8_out};  // Bit_Extender bit_extender_48
  assign srliImmSel = {{2{1'b0}}, and_9_out};  // Bit_Extender bit_extender_49
  Shifter #(.width(4)) shifter_17 (.in(bit_extender_39_out), .\dist (2'b10), .out(oriALUSel));
  assign oriImmSel = {{2{1'b0}}, and_10_out};  // Bit_Extender bit_extender_50
  assign andiALUSel = bit_extender_41_out | shifter_18_out;  // OR_Gate or_11, 4 bits wide
  Shifter #(.width(4)) shifter_18 (.in(bit_extender_41_out), .\dist (2'b01), .out(shifter_18_out));
  assign bit_extender_51_out = {{2{1'b0}}, Lui};  // Bit_Extender bit_extender_51
  not not_78 (LuiASel, Lui);
  not not_79 (LuiMemRW, Lui);
  assign LuiWBSel = {{1{1'b0}}, Lui};  // Bit_Extender bit_extender_52
  Multiplexer #(.width(32)) multiplexer_10 (.in0(R1), .out(multiplexer_10_out), .sel(ASel));  // open: in1, en
  Negator #(.width(32)) negator_1 (.in(multiplexer_9_out), .out(negator_1_out));
  control_unit Control_Unit (
    .Instruction(INSTRUCTION), .brEQ(brEQ), .brLT(brLT), .JALRtype(Jalr), .JALtype(Jal), .LUItype(Lui),
    .BLTUtype(Bltu), .BLTtype(Blt), .BEQtype(Beq), .SWtype(Sw), .ANDItype(Andi), .ORItype(Ori),
    .SRLItype(Srli), .XORItype(Xori), .SLTItype(Slti), .SLLItype(Slli), .ADDItype(Addi), .LWtype(Lb),
    .LHtype(Lh), .LBtype(Lb), .ANDtype(And), .REMtype(Rem), .ORtype(Or), .SRLtype(Srl), .DIVtype(Div),
    .XORtype(Xor), .SLTtype(Slt), .MULHtype(MulH), .SLLtype(Sll), .SUBtype(NegSel), .MULtype(Mul),
    .ADDtype(Add));  // open: brEQ_2, brLT_2
  assign sltiALUSel = shifter_15_out | shifter_19_out;  // OR_Gate or_12, 4 bits wide
  Shifter #(.width(4)) shifter_19 (.in(bit_extender_33_out), .\dist (2'b10), .out(shifter_19_out));
  assign xoriALUSel = bit_extender_35_out | shifter_16_out;  // OR_Gate or_13, 4 bits wide
  Shifter #(.width(3)) shifter_20 (.in(bit_extender_51_out), .\dist (2'b01), .out(shifter_20_out));
  Shifter #(.width(4)) shifter_21 (.in(bit_extender_46_out), .\dist (2'b01), .out(LuiALUSel));
  Multiplexer #(.width(32)) multiplexer_11 (
    .in0(multiplexer_10_out), .in1({32{1'b0}}), .out(multiplexer_11_out), .sel(Lui));  // open: en
  alu_main main_2 (
    .Switch(ALUSel), .X(multiplexer_11_out), .Result(main_2_result), .Y(multiplexer_12_out));  // open: Equal
  Multiplexer #(.width(32)) multiplexer_12 (
    .in0(multiplexer_9_out), .in1(negator_1_out), .out(multiplexer_12_out), .sel(NegSel));  // open: en
  Demultiplexer demultiplexer_4 (.out0(demultiplexer_4_out0), .out1(BeqPCSel), .in(Beq), .en(brEQ));  // open: sel
  Demultiplexer demultiplexer_5 (.out0(demultiplexer_5_out0), .out1(BltPCSel), .in(Blt), .en(brLT));  // open: sel
  Demultiplexer demultiplexer_6 (.out0(demultiplexer_6_out0), .out1(BltuPCSel), .in(Bltu), .en(brLT));  // open: sel
  assign LuiiImmSel = bit_extender_51_out | shifter_20_out;  // OR_Gate or_14, 3 bits wide
  Multiplexer multiplexer_13 (.in0(1'b0), .in1(1'b1), .out(MemRW), .sel(Sw));  // open: en
  not not_80 (lbPCSel, Lb);
  not not_81 (lbASel, Lb);
  not not_82 (lbMemRW, Lb);
  not not_83 (not_83_out, Lb);
  not not_84 (lwPCSel, Lb);
  not not_85 (lwASel, Lb);
  not not_86 (lwMemRW, Lb);
  not not_87 (not_87_out, Lb);
  not not_88 (BeqPCSel, demultiplexer_4_out0);
  not not_89 (BltPCSel, demultiplexer_5_out0);
  not not_90 (BltuPCSel, demultiplexer_6_out0);
  not not_91 (not_91_out, Jal);
  // mem_main MEM: pin names not known; wires that end beside it: MEM_p1, MEM_p2, MEM_p2, MEM_p4, main_2_result, R2, MemRW, MEM_p4, CLOCK, MEM_p10, MEM_p11
  assign bit_extender_53_out = {{1{1'b0}}, Lb};  // Bit_Extender bit_extender_53
  Shifter #(.width(2)) shifter_22 (.in(bit_extender_53_out), .\dist (1'b1), .out(lbWBSel));
  and and_13 (and_13_out, not_83_out, Lb);
  assign bit_extender_54_out = {{1{1'b0}}, Lb};  // Bit_Extender bit_extender_54
  not not_92 (lhPCSel, Lh);
  not not_93 (lhASel, Lh);
  not not_94 (lhMemRW, Lh);
  not not_95 (not_95_out, Lh);
  not not_96 (SwPCSel, Sw);
  not not_97 (SwASel, Sw);
  assign bit_extender_55_out = {{3{1'b0}}, Sw};  // Bit_Extender bit_extender_55
  not not_98 (SwRegWEn, Sw);
  assign SwWBSel = {{1{1'b0}}, Sw};  // Bit_Extender bit_extender_56
  assign swImmSel = {{2{1'b0}}, Sw};  // Bit_Extender bit_extender_57
  assign bit_extender_58_out = {{2{1'b0}}, Jal};  // Bit_Extender bit_extender_58
  assign bit_extender_59_out = {{3{1'b0}}, Jal};  // Bit_Extender bit_extender_59
  not not_99 (JalMemRW, Jal);
  assign JalWBSel = {{1{1'b0}}, not_91_out};  // Bit_Extender bit_extender_60
  assign bit_extender_61_out = {{3{1'b0}}, Jalr};  // Bit_Extender bit_extender_61
  not not_100 (JalrMemRW, Jalr);
  not not_101 (not_101_out, Jalr);
  assign bit_extender_62_out = {{3{1'b0}}, Lb};  // Bit_Extender bit_extender_62
  assign lbImmSel = {{2{1'b0}}, and_13_out};  // Bit_Extender bit_extender_63
  assign bit_extender_64_out = {{3{1'b0}}, Lb};  // Bit_Extender bit_extender_64
  Shifter #(.width(2)) shifter_23 (.in(bit_extender_54_out), .\dist (1'b1), .out(lwWBSel));
  and and_14 (and_14_out, not_87_out, Lb);
  assign bit_extender_65_out = {{1{1'b0}}, Lh};  // Bit_Extender bit_extender_65
  and and_15 (and_15_out, not_95_out, Lh);
  Shifter #(.width(4)) shifter_24 (.in(bit_extender_55_out), .\dist (2'b01), .out(SwALUSel));
  assign bit_extender_66_out = {{3{1'b0}}, Beq};  // Bit_Extender bit_extender_66
  not not_102 (BeqMemRW, Beq);
  not not_103 (BeqRegWEn, Beq);
  assign BeqWBSel = {{1{1'b0}}, Beq};  // Bit_Extender bit_extender_67
  assign bit_extender_68_out = {{3{1'b0}}, Blt};  // Bit_Extender bit_extender_68
  assign BltWBSel = {{1{1'b0}}, Blt};  // Bit_Extender bit_extender_69
  Shifter #(.width(3)) shifter_25 (.in(bit_extender_58_out), .\dist (2'b10), .out(JaliImmSel));
  Shifter #(.width(4)) shifter_26 (.in(bit_extender_59_out), .\dist (2'b01), .out(JalALUSel));
  not not_104 (not_104_out, Jalr);
  not not_105 (JalrASel, Jalr);
  Shifter #(.width(4)) shifter_27 (.in(bit_extender_61_out), .\dist (2'b01), .out(JalrALUSel));
  assign JalrWBSel = {{1{1'b0}}, not_101_out};  // Bit_Extender bit_extender_70
  Multiplexer #(.select(2), .width(32)) multiplexer_14 (
    .in0(adder_1_out), .in1(main_2_result), .in2(MEM_p11), .out(multiplexer_14_out), .sel(WBSel));  // open: in3, en
  Shifter #(.width(4)) shifter_28 (.in(bit_extender_62_out), .\dist (2'b01), .out(lbALUSel));
  assign lwImmSel = {{2{1'b0}}, and_14_out};  // Bit_Extender bit_extender_71
  assign bit_extender_72_out = {{3{1'b0}}, Lh};  // Bit_Extender bit_extender_72
  Shifter #(.width(2)) shifter_29 (.in(bit_extender_65_out), .\dist (1'b1), .out(lhWBSel));
  assign lhImmSel = {{2{1'b0}}, and_15_out};  // Bit_Extender bit_extender_73
  assign bit_extender_74_out = {{2{1'b0}}, Beq};  // Bit_Extender bit_extender_74
  Shifter #(.width(4)) shifter_30 (.in(bit_extender_66_out), .\dist (2'b01), .out(BeqALUSel));
  assign bit_extender_75_out = {{2{1'b0}}, Blt};  // Bit_Extender bit_extender_75
  not not_106 (BltMemRW, Blt);
  not not_107 (BltRegWEn, Blt);
  assign bit_extender_76_out = {{2{1'b0}}, Bltu};  // Bit_Extender bit_extender_76
  assign bit_extender_77_out = {{3{1'b0}}, Bltu};  // Bit_Extender bit_extender_77
  not not_108 (BltuMemRW, Bltu);
  not not_109 (BltuRegWEn, Bltu);
  assign BltuWBSel = {{1{1'b0}}, Bltu};  // Bit_Extender bit_extender_78
  and and_16 (and_16_out, not_104_out, Jalr);
  Shifter #(.width(4)) shifter_31 (.in(bit_extender_64_out), .\dist (2'b01), .out(lwALUSel));
  Shifter #(.width(4)) shifter_32 (.in(bit_extender_72_out), .\dist (2'b01), .out(lhALUSel));
  Shifter #(.width(3)) shifter_33 (.in(bit_extender_74_out), .\dist (2'b01), .out(BeqiImmSel));
  Shifter #(.width(3)) shifter_34 (.in(bit_extender_75_out), .\dist (2'b01), .out(BltiImmSel));
  Shifter #(.width(4)) shifter_35 (.in(bit_extender_68_out), .\dist (2'b01), .out(BltALUSel));
  Shifter #(.width(3)) shifter_36 (.in(bit_extender_76_out), .\dist (2'b01), .out(BltuiImmSel));
  Shifter #(.width(4)) shifter_37 (.in(bit_extender_77_out), .\dist (2'b01), .out(BltuALUSel));
  assign JalrImmSel = {{2{1'b0}}, and_16_out};  // Bit_Extender bit_extender_79

  // Other names for the same wires on the sheet: a0[31:0] = a0_Value; addiBSel = Addi; addiRegWEn = Addi;
  //   addRegWEn = Add; andiBSel = Andi; andiRegWEn = Andi; andRegWEn = And; BeqASel = Beq; BeqBSel = Beq;
  //   BltASel = Blt; BltBSel = Blt; BltuASel = Bltu; BltuBSel = Bltu; clk = CLOCK; divRegWEn = Div;
  //   fetch_addr[31:0] = FETCH_ADDRESS; JalASel = Jal; JalBSel = Jal; JalPCSel = Jal; JalRegWEn = Jal;
  //   JalrBSel = Jalr; JalrPCSel = Jalr; JalrRegWEn = Jalr; lhBSel = Lh; lhRegWEn = Lh; LuiBSel = Lui;
  //   LuiRegWEn = Lui; LuiSel = Lui; lbRegWEn = Lb; Lw = Lb; lwBSel = Lb; lwRegWEn = Lb; mulhRegWEn = MulH;
  //   mulRegWEn = Mul; oriBSel = Ori; oriRegWEn = Ori; orRegWEn = Or; ra[31:0] = ra_Value; remRegWEn = Rem;
  //   s0[31:0] = s0_Value; s1[31:0] = s1_Value; slliBSel = Slli; slliRegWEn = Slli; sllRegWEn = Sll; sltiBSel = Slti;
  //   sltiRegWEn = Slti; sltRegWEn = Slt; sp[31:0] = sp_Value; srliBSel = Srli; srliRegWEn = Srli; srlRegWEn = Srl;
  //   Sub = NegSel; subRegWEn = NegSel; SwBSel = Sw; SwMemRW = Sw; t0[31:0] = t0_Value; t1[31:0] = t1_Value;
  //   xoriBSel = Xori; xoriRegWEn = Xori; xorRegWEn = Xor

  // Notes on the sheet:
  //   Output
  //   These are outputs/inputs from run.circ
  //   Inputs
  //   These are DEBUG/TEST outputs from your circuit.
endmodule

module control_unit (
  input  [31:0] Instruction,
  input  brEQ,
  input  brLT,
  output JALRtype,
  output JALtype,
  output LUItype,
  output BLTUtype,
  output BLTtype,
  output BEQtype,
  output SWtype,
  output ANDItype,
  output ORItype,
  output SRLItype,
  output XORItype,
  output SLTItype,
  output SLLItype,
  output ADDItype,
  output LWtype,
  output LHtype,
  output LBtype,
  output ANDtype,
  output REMtype,
  output ORtype,
  output SRLtype,
  output DIVtype,
  output XORtype,
  output SLTtype,
  output MULHtype,
  output SLLtype,
  output SUBtype,
  output MULtype,
  output ADDtype,
  output brEQ_2,
  output brLT_2
);

  wire demultiplexer_1_out0, demultiplexer_1_out1, demultiplexer_2_out0, demultiplexer_3_out0,
       demultiplexer_4_out0, demultiplexer_4_out1, demultiplexer_5_out1, demultiplexer_6_out0,
       demultiplexer_9_out1, demultiplexer_11_out0, demultiplexer_11_out1, demultiplexer_12_out0,
       demultiplexer_12_out1, demultiplexer_13_out0, demultiplexer_13_out1, demultiplexer_16_out0,
       demultiplexer_16_out1, demultiplexer_17_out0, demultiplexer_17_out1, demultiplexer_18_out0,
       demultiplexer_18_out1, demultiplexer_20_out0, demultiplexer_21_out0, demultiplexer_21_out1,
       demultiplexer_22_out0, demultiplexer_22_out1, demultiplexer_23_out0, demultiplexer_23_out1,
       demultiplexer_24_out0, demultiplexer_24_out1, demultiplexer_26_out0, Itype, LoadItype, Rtype;

  Demultiplexer demultiplexer_1 (
    .out0(demultiplexer_1_out0), .out1(demultiplexer_1_out1), .in(1'b1), .sel(Instruction[6]));  // open: en
  Demultiplexer demultiplexer_2 (
    .out0(demultiplexer_2_out0), .out1(JALtype), .in(demultiplexer_1_out1), .sel(Instruction[3]));  // open: en
  Demultiplexer demultiplexer_3 (
    .out0(demultiplexer_3_out0), .out1(Itype), .in(demultiplexer_4_out0), .sel(Instruction[4]));  // open: en
  Demultiplexer demultiplexer_4 (
    .out0(demultiplexer_4_out0), .out1(demultiplexer_4_out1), .in(demultiplexer_1_out0), .sel(Instruction[5]));  // open: en
  Demultiplexer demultiplexer_5 (
    .out0(SWtype), .out1(demultiplexer_5_out1), .in(demultiplexer_4_out1), .sel(Instruction[4]));  // open: en
  Demultiplexer demultiplexer_6 (
    .out0(demultiplexer_6_out0), .out1(JALRtype), .in(demultiplexer_2_out0), .sel(Instruction[2]));  // open: en
  Demultiplexer demultiplexer_7 (
    .out0(Rtype), .out1(LUItype), .in(demultiplexer_5_out1), .sel(Instruction[2]));  // open: en
  Demultiplexer demultiplexer_8 (.out1(LoadItype), .in(demultiplexer_3_out0), .sel(Instruction[1]));  // open: out0, en
  Demultiplexer demultiplexer_9 (
    .out0(BEQtype), .out1(demultiplexer_9_out1), .in(demultiplexer_6_out0), .sel(Instruction[14]));  // open: en
  Demultiplexer demultiplexer_10 (
    .out0(BLTtype), .out1(BLTUtype), .in(demultiplexer_9_out1), .sel(Instruction[13]));  // open: en
  Demultiplexer demultiplexer_11 (
    .out0(demultiplexer_11_out0), .out1(demultiplexer_11_out1), .in(demultiplexer_12_out0),
    .sel(Instruction[13]));  // open: en
  Demultiplexer demultiplexer_12 (
    .out0(demultiplexer_12_out0), .out1(demultiplexer_12_out1), .in(Itype), .sel(Instruction[14]));  // open: en
  Demultiplexer demultiplexer_13 (
    .out0(demultiplexer_13_out0), .out1(demultiplexer_13_out1), .in(demultiplexer_12_out1),
    .sel(Instruction[13]));  // open: en
  Demultiplexer demultiplexer_14 (
    .out0(ADDItype), .out1(SLLItype), .in(demultiplexer_11_out0), .sel(Instruction[12]));  // open: en
  Demultiplexer demultiplexer_15 (
    .out0(XORItype), .out1(SRLItype), .in(demultiplexer_13_out0), .sel(Instruction[12]));  // open: en
  Demultiplexer demultiplexer_16 (
    .out0(demultiplexer_16_out0), .out1(demultiplexer_16_out1), .in(demultiplexer_17_out0),
    .sel(Instruction[13]));  // open: en
  Demultiplexer demultiplexer_17 (
    .out0(demultiplexer_17_out0), .out1(demultiplexer_17_out1), .in(Rtype), .sel(Instruction[14]));  // open: en
  Demultiplexer demultiplexer_18 (
    .out0(demultiplexer_18_out0), .out1(demultiplexer_18_out1), .in(demultiplexer_17_out1),
    .sel(Instruction[13]));  // open: en
  Demultiplexer demultiplexer_19 (
    .out0(SLTItype), .in(demultiplexer_11_out1), .sel(Instruction[12]));  // open: out1, en
  Demultiplexer demultiplexer_20 (
    .out0(demultiplexer_20_out0), .out1(LWtype), .in(LoadItype), .sel(Instruction[13]));  // open: en
  Demultiplexer demultiplexer_21 (
    .out0(demultiplexer_21_out0), .out1(demultiplexer_21_out1), .in(demultiplexer_16_out0),
    .sel(Instruction[12]));  // open: en
  Demultiplexer demultiplexer_22 (
    .out0(demultiplexer_22_out0), .out1(demultiplexer_22_out1), .in(demultiplexer_16_out1),
    .sel(Instruction[12]));  // open: en
  Demultiplexer demultiplexer_23 (
    .out0(demultiplexer_23_out0), .out1(demultiplexer_23_out1), .in(demultiplexer_18_out0),
    .sel(Instruction[12]));  // open: en
  Demultiplexer demultiplexer_24 (
    .out0(demultiplexer_24_out0), .out1(demultiplexer_24_out1), .in(demultiplexer_18_out1),
    .sel(Instruction[12]));  // open: en
  Demultiplexer demultiplexer_25 (
    .out0(ORItype), .out1(ANDItype), .in(demultiplexer_13_out1), .sel(Instruction[12]));  // open: en
  Demultiplexer demultiplexer_26 (
    .out0(demultiplexer_26_out0), .out1(SUBtype), .in(demultiplexer_21_out0), .sel(Instruction[30]));  // open: en
  Demultiplexer demultiplexer_27 (
    .out0(SLLtype), .out1(MULHtype), .in(demultiplexer_21_out1), .sel(Instruction[25]));  // open: en
  Demultiplexer demultiplexer_28 (.out0(SLTtype), .in(demultiplexer_22_out0), .sel(Instruction[25]));  // open: out1, en
  Demultiplexer demultiplexer_29 (.in(demultiplexer_22_out1), .sel(Instruction[25]));  // open: out0, out1, en
  Demultiplexer demultiplexer_30 (
    .out0(XORtype), .out1(DIVtype), .in(demultiplexer_23_out0), .sel(Instruction[25]));  // open: en
  Demultiplexer demultiplexer_31 (.out0(SRLtype), .in(demultiplexer_23_out1), .sel(Instruction[25]));  // open: out1, en
  Demultiplexer demultiplexer_32 (
    .out0(ORtype), .out1(REMtype), .in(demultiplexer_24_out0), .sel(Instruction[25]));  // open: en
  Demultiplexer demultiplexer_33 (.out0(ANDtype), .in(demultiplexer_24_out1), .sel(Instruction[25]));  // open: out1, en
  Demultiplexer demultiplexer_34 (
    .out0(LBtype), .out1(LHtype), .in(demultiplexer_20_out0), .sel(Instruction[12]));  // open: en
  Demultiplexer demultiplexer_35 (
    .out0(ADDtype), .out1(MULtype), .in(demultiplexer_26_out0), .sel(Instruction[25]));  // open: en

  assign brEQ_2 = brEQ;
  assign brLT_2 = brLT;

  // Other names for the same wires on the sheet: Op1 = Instruction[1]; Op2 = Instruction[2]; Op3 = Instruction[3];
  //   Op4 = Instruction[4]; Op5 = Instruction[5]; Op6 = Instruction[6]; Func3_12 = Instruction[12];
  //   Func3_13 = Instruction[13]; Func3_14 = Instruction[14]; Func7_25 = Instruction[25]; Func7_30 = Instruction[30]

  // Notes on the sheet:
  //   ITypes
  //   UJTypes
  //   UTypes
  //   SBTypes
  //   STypes
  //   ITypes
  //   RTypes
endmodule
