// Logisim project alu.circ as structural Verilog: 1 circuit, main circuit main
module main (
  input  [31:0] X,
  input  [31:0] Y,
  input  [3:0] Switch,
  output Equal,
  output [31:0] Result
);

  wire comparator_1_lt;
  wire [4:0] bit_extender_1_out, bit_extender_2_out;
  wire [31:0] add, \and , div, mult, multh, \or , rem, sll, slt, srl, \xor ;

  Bit_Extender #(.in_width(32), .out_width(5)) bit_extender_1 (.in(Y), .out(bit_extender_1_out));
  Bit_Extender #(.in_width(32), .out_width(5)) bit_extender_2 (.in(Y), .out(bit_extender_2_out));
  Adder #(.width(32)) adder_1 (.a(X), .b(Y), .out(add));  // open: cin, cout
  assign \and  = X & Y;  // AND_Gate and_1, 32 bits wide
  assign \or  = X | Y;  // OR_Gate or_1, 32 bits wide
  assign \xor  = X ^ Y;  // XOR_Gate xor_1, 32 bits wide
  Comparator #(.width(32), .mode("unsigned")) comparator_1 (
    .a(X), .b(Y), .eq(Equal), .lt(comparator_1_lt));  // open: gt
  Shifter #(.width(32)) shifter_1 (.in(X), .\dist (bit_extender_1_out), .out(sll));
  Shifter #(.width(32), .shift("lr")) shifter_2 (.in(X), .\dist (bit_extender_2_out), .out(srl));
  assign slt = {{31{1'b0}}, comparator_1_lt};  // Bit_Extender bit_extender_3
  Multiplier #(.width(32)) multiplier_1 (.a(X), .b(Y), .out(mult), .cout(multh));  // open: cin
  Divider #(.width(32)) divider_1 (.a(X), .b(Y), .out(div), .rem(rem));  // open: upper
  Multiplexer #(.select(4), .width(32)) multiplexer_1 (
    .in0(sll), .in1(srl), .in2(add), .in3(\and ), .in4(\or ), .in5(\xor ), .in6(slt), .in7(mult),
    .in8(multh), .in9(div), .in10(rem), .out(Result), .sel(Switch));  // open: in11, in12, in13, in14, in15, en

  // Other names for the same wires on the sheet: S[3:0] = Switch

  // Notes on the sheet:
  //   INPUTS to your circuit
  //   DON'T CHANGE THE LOCATIONS OF THE INPUTS AND OUTPUTS!
  //   OUTPUTS from your circuit
endmodule
