// Logisim project regfile.circ as structural Verilog: 1 circuit, main circuit main
module main (
  input  [4:0] Read_Register_1__rs1,
  input  [4:0] Read_Register_2__rs2,
  input  [4:0] Write_Register__rd,
  input  [31:0] Write_Data,
  input  Write_Enable,
  input  Clock,
  output [31:0] s0_Value,
  output [31:0] s1_Value,
  output [31:0] t0_Value,
  output [31:0] t1_Value,
  output [31:0] a0_Value,
  output [31:0] ra_Value,
  output [31:0] sp_Value,
  output [31:0] Read_Data_1,
  output [31:0] Read_Data_2
);

  wire clock_1_out, enx0, enx1, enx2, enx5, enx6, enx8, enx9, enx10, enx11;
  wire [31:0] a1, datax0, datax1, datax2, datax5, datax6, datax8, datax9, datax10, datax11, zero;

  Demultiplexer #(.select(5)) demultiplexer_1 (
    .out0(enx0), .out1(enx1), .out2(enx2), .out3(enx5), .out4(enx6), .out5(enx8), .out6(enx9), .out7(enx10),
    .out8(enx11), .in(Write_Enable), .sel(Write_Register__rd));  // open: out9, out10, out11, out12, out13, out14, out15, out16, out17, out18, out19, out20, out21, out22, out23, out24, out25, out26, out27, out28, out29, out30, out31, en
  Register #(.width(32)) register_1 (.Q(zero), .clk(clock_1_out));  // open: D, en, clr
  Register #(.width(32)) register_2 (.D(datax1), .en(enx1), .Q(ra_Value), .clk(clock_1_out));  // open: clr
  Demultiplexer #(.select(5), .width(32)) demultiplexer_2 (
    .out0(datax0), .out1(datax1), .out2(datax2), .out3(datax5), .out4(datax6), .out5(datax8), .out6(datax9),
    .out7(datax10), .out8(datax11), .in(Write_Data), .sel(Write_Register__rd), .en(Write_Enable));  // open: out9, out10, out11, out12, out13, out14, out15, out16, out17, out18, out19, out20, out21, out22, out23, out24, out25, out26, out27, out28, out29, out30, out31
  Register #(.width(32)) register_3 (.D(datax2), .en(enx2), .Q(sp_Value), .clk(clock_1_out));  // open: clr
  Register #(.width(32)) register_4 (.D(datax5), .en(enx5), .Q(t0_Value), .clk(clock_1_out));  // open: clr
  Clock clock_1 (.out(clock_1_out));
  Register #(.width(32)) register_5 (.D(datax6), .en(enx6), .Q(t1_Value), .clk(clock_1_out));  // open: clr
  Register #(.width(32)) register_6 (.D(datax8), .en(enx8), .Q(s0_Value), .clk(clock_1_out));  // open: clr
  Multiplexer #(.select(5), .width(32)) multiplexer_1 (
    .in0(zero), .in1(ra_Value), .in2(sp_Value), .in3(t0_Value), .in4(t1_Value), .in5(s0_Value),
    .in6(s1_Value), .in7(a0_Value), .in8(a1), .out(Read_Data_1), .sel(Read_Register_1__rs1));  // open: in9, in10, in11, in12, in13, in14, in15, in16, in17, in18, in19, in20, in21, in22, in23, in24, in25, in26, in27, in28, in29, in30, in31, en
  Register #(.width(32)) register_7 (.D(datax9), .en(enx9), .Q(s1_Value), .clk(clock_1_out));  // open: clr
  Register #(.width(32)) register_8 (.D(datax10), .en(enx10), .Q(a0_Value), .clk(clock_1_out));  // open: clr
  Multiplexer #(.select(5), .width(32)) multiplexer_2 (
    .in0(zero), .in1(ra_Value), .in2(sp_Value), .in3(t0_Value), .in4(t1_Value), .in5(s0_Value),
    .in6(s1_Value), .in7(a0_Value), .in8(a1), .out(Read_Data_2), .sel(Read_Register_2__rs2));  // open: in9, in10, in11, in12, in13, in14, in15, in16, in17, in18, in19, in20, in21, in22, in23, in24, in25, in26, in27, in28, in29, in30, in31, en
  Register #(.width(32)) register_9 (.D(datax11), .en(enx11), .Q(a1), .clk(clock_1_out));  // open: clr

  // Other names for the same wires on the sheet: a0[31:0] = a0_Value; clk = Clock; ra[31:0] = ra_Value;
  //   read_data1[31:0] = Read_Data_1; read_data2[31:0] = Read_Data_2; read_reg1[4:0] = Read_Register_1__rs1;
  //   read_reg2[4:0] = Read_Register_2__rs2; s0[31:0] = s0_Value; s1[31:0] = s1_Value; sp[31:0] = sp_Value;
  //   t0[31:0] = t0_Value; t1[31:0] = t1_Value; write_en = Write_Enable; write_reg[4:0] = Write_Register__rd

  // Notes on the sheet:
  //   INPUTS to your circuit
  //   These are DEBUG/TEST outputs from your circuit.
  //   DON'T CHANGE THE LOCATIONS OF THE INPUTS AND OUTPUTS!
  //   OUTPUTS from your circuit
endmodule
